# Fritzing sketch vib_belt_nano (saved by Fritzing 0.9.2b)

parts:
  Power_plug1 = Power plug
  U2 = Vibration Motor- ROB-08449 [package=vibe-motor-10mm]
  U1 = Vibration Motor- ROB-08449 [package=vibe-motor-10mm]
  Part2 = Arduino Nano (Rev3.0)
  R1 = Resistor [tolerance=±5% resistance=100 package="1206 [SMD]"]
  R2 = Resistor [tolerance=±5% resistance=5.1k package="1206 [SMD]"]
  C1 = Ceramic Capacitor [capacitance="100 nF" package="1206 [SMD, multilayer]"]
  Q1 = NPN-Transistor [package="SOT-23 [SMD]"]
  D2 = Schottky Diode [part_number=1N5817 package="Melf DO-213 AB [SMD]"]
  J1 = female pin header, 3 pins [form="♀ (female)"]
  J2 = female pin header, 3 pins [form="♀ (female)"]
  U3 = Vibration Motor- ROB-08449 [package=vibe-motor-10mm]
  J3 = female pin header, 3 pins [form="♀ (female)"]
  J5 = female pin header, 3 pins [form="♀ (female)"]
  J7 = female pin header, 3 pins [form="♀ (female)"]
  J9 = female pin header, 3 pins [form="♀ (female)"]
  J11 = female pin header, 3 pins [form="♀ (female)"]
  J13 = female pin header, 3 pins [form="♀ (female)"]
  J14 = female pin header, 3 pins [form="♀ (female)"]
  J15 = female pin header, 3 pins [form="♀ (female)"]
  J16 = female pin header, 3 pins [form="♀ (female)"]
  J17 = female pin header, 3 pins [form="♀ (female)"]
  J18 = female pin header, 3 pins [form="♀ (female)"]
  J19 = female pin header, 3 pins [form="♀ (female)"]
  U4 = Vibration Motor- ROB-08449 [package=vibe-motor-10mm]
  U5 = Vibration Motor- ROB-08449 [package=vibe-motor-10mm]
  U6 = Vibration Motor- ROB-08449 [package=vibe-motor-10mm]
  U7 = Vibration Motor- ROB-08449 [package=vibe-motor-10mm]
  U8 = Vibration Motor- ROB-08449 [package=vibe-motor-10mm]
  U9 = Vibration Motor- ROB-08449 [package=vibe-motor-10mm]
  U10 = Vibration Motor- ROB-08449 [package=vibe-motor-10mm]
  U11 = Vibration Motor- ROB-08449 [package=vibe-motor-10mm]
  U12 = Vibration Motor- ROB-08449 [package=vibe-motor-10mm]
  U13 = Vibration Motor- ROB-08449 [package=vibe-motor-10mm]
  U14 = Vibration Motor- ROB-08449 [package=vibe-motor-10mm]
  J20 = female pin header, 1 pin [form="♀ (female)"]

nets:
  GND: Power_plug1.GND, Part2.GND, J3.pin1, J5.pin1, J7.pin1, J9.pin1, J11.pin1, J13.pin1, J14.pin1, J15.pin1, J16.pin1, J17.pin1, J18.pin1, J19.pin1
  N1: Power_plug1.VCC, U3.-, J3.pin2, J5.pin2, J7.pin2, J9.pin2, J11.pin2, J13.pin2, J14.pin2, J15.pin2, J16.pin2, J17.pin2, J18.pin2, J19.pin2, U4.-, U5.-, U6.-, U7.-, U8.-, U9.-, U10.-, U11.-, U12.-, U13.-, U14.-
  N2: U2.+, J2.pin3
  N3: U2.-, J2.pin2
  N4: U1.+, R1.Pin_1, C1.1, D2.anode
  N5: U1.-, C1.0, D2.cathode, J1.pin2
  N6: Part2.D3, U3.+, J3.pin3, J14.pin3, U4.+
  N7: Part2.D5, J5.pin3, J15.pin3, U5.+, U6.+
  N8: Part2.D6, J7.pin3, J16.pin3, U7.+, U8.+
  N9: Part2.D9, J9.pin3, J17.pin3, U9.+, U10.+
  N10: Part2.D10, J11.pin3, J18.pin3, U11.+, U12.+
  N11: Part2.D11/MOSI, J13.pin3, J19.pin3, U13.+, U14.+
  N12: R1.Pin_0, Q1.1
  N13: R2.Pin_0, Q1.0, J1.pin3
  N14: R2.Pin_1, Q1.2, J1.pin1
  N15: J2.pin1, J20.pin1

notes:
  Considering Vibration Motor's red cable as + and black as -
  5Vdc input
  Gnd Vcc Sig
  Approximate schematic of Landa Tianrui HM0019
  Simplified schematic for use in the circuit
  <=====>
